# Fritzing sketch SL-1255_Nano (saved by Fritzing 0.9.2b)
breadboards: 1

parts:
  Part1 = Arduino Nano (Rev3.0)
  R7 = Resistor [tolerance=±5% resistance=470 package=THT]
  R5 = Resistor [tolerance=±5% resistance=470 package=THT]
  R6 = Resistor [tolerance=±5% resistance=470 package=THT]
  R14 = Resistor [tolerance=±5% resistance=470 package=THT]
  R13 = Resistor [tolerance=±5% resistance=470 package=THT]
  R12 = Resistor [tolerance=±5% resistance=470 package=THT]  # not connected
  R11 = Resistor [tolerance=±5% resistance=470 package=THT]
  R10 = Resistor [tolerance=±5% resistance=470 package=THT]
  R9 = Resistor [tolerance=±5% resistance=470 package=THT]
  R4 = Resistor [tolerance=±5% resistance=470 package=THT]
  R3 = Resistor [tolerance=±5% resistance=470 package=THT]
  R8 = Resistor [tolerance=±5% resistance=470 package=THT]  # not connected
  R1 = Resistor [tolerance=±5% resistance=470 package=THT]
  R2 = Resistor [tolerance=±5% resistance=470 package=THT]
  U2 = 7-SEGMENT-DISPLAY-1_-RED [package=7-segment-1_pth]
  U1 = 7-SEGMENT-DISPLAY-1_-RED [package=7-segment-1_pth]

nets:
  N1: Part1.D2, R7.Pin_0
  N2: Part1.D3, R6.Pin_0
  N3: Part1.D4, R5.Pin_0
  N4: Part1.D5, R4.Pin_0
  N5: Part1.D6, R3.Pin_0
  N6: Part1.D7, R2.Pin_0
  N7: Part1.D8, R1.Pin_0
  N8: Part1.D9, R14.Pin_0
  N9: Part1.D12/MISO, R11.Pin_0
  N10: Part1.A0, R9.Pin_0
  N11: Part1.D13/SCK, R10.Pin_0
  N12: R7.Pin_1, U2.G
  N13: R6.Pin_1, U2.G2
  N14: R14.Pin_1, U1.B
  N15: R13.Pin_1, U1.G2
  N16: R11.Pin_1, U1.C
  N17: R10.Pin_1, U1.DP
  N18: R9.Pin_1, U1.A
  N19: R4.Pin_1, U2.D
  N20: R2.Pin_1, U2.F
  N21: U2.G1, U1.G1
